# Fritzing sketch Peso_Bill_To_Chit (saved by Fritzing 0.9.3b)
breadboards: 1

parts:
  U1 = ESP32S-HiLetgo [part_number=ESP32S-HiLetgo]
  Part1 = Coin Acceptor - 6-Coin version
  A1 = Bill acceptor TB74-U
  J1 = Basic Servo
  J2 = Basic Servo
  J3 = Basic Servo
  J4 = Basic Servo
  Part2 = 16-Channel 12-bit PWM Servo Driver - I2C [part_number=815]
  HLK-PM1 = HLK-PM12 [part_number=HLK-PM12]
  M1 = RioRand LM2596

nets:
  N1: U1.3.3, Part2.VCC
  N2: U1.GPIO26, Part1.SIG
  GND: U1.GND, Part1.GND, A1.Pin_1, A1.Pin_2, A1.Pin_3, A1.Pin_4, J1.gnd, J2.gnd, J3.gnd, J4.gnd, Part2.GND, HLK-PM1.-Vo, M1.Pin_1, M1.Pin_4
  VCC: U1.VIN, J1.vcc, J2.vcc, J3.vcc, J4.vcc, Part2.5.0V, M1.Pin_3
  N3: U1.GPIO19, A1.Pin_5
  N4: U1.GPIO3, Part2.SDA
  N5: U1.GPIO23, Part2.SCL
  N6: Part1.12V, A1.Pin_6, A1.Pin_10, HLK-PM1.+Vo, M1.Pin_2
  N7: J1.pulse, Part2.PWM0
  N8: J2.pulse, Part2.PWM1
  N9: J3.pulse, Part2.PWM2
  N10: J4.pulse, Part2.PWM3

custom parts:
  ESP32S-HiLetgo: HiLetgo ESP-WROOM-32 ESP32 ESP-32S Development Board 2.4GHz Dual-Mode WiFi + Bluetooth Dual Cores Microcontroller The ESP32 integrated with Antenna switches, RF Balun, power amplifiers, low-noise amplifiers, filters, and management modules, and the entire solution occupies the least area of PCB. 2.4 GHz Wi-Fi plus Bluetooth dual-mode chip, with TSMC Ultra-low power consumption 40nm technology,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
  Coin Acceptor - 6-Coin version: 12V coin acceptor that can handle up to 6 different denominations. Output is either pulse width, serial, or single pin per coin value.
  Bill acceptor TB74-U: The TB-Series is the latest generation of banknote reader designed exclusively by TOPVME with the highest safety and acceptance rate have over 96%.
  16-Channel 12-bit PWM Servo Driver - I2C: You want to make a cool robot, maybe a hexapod walker, or maybe just a piece of art with a lot of moving parts. Or maybe you want to drive a lot of LEDs with precise PWM output. Using only two pins, control 16 free-running PWM outputs! You can even chain up 62 breakouts to control up to 992 PWM outputs.
